# Fritzing sketch iot-device-schema (saved by Fritzing 0.9.5d)

parts:
  Raspberry_Pi_2 = Raspberry Pi 3 [part_number=RPI-3-V1.2]
  Part1 = LCD1602-I2C
  Mod1 = KY-004 Key Switch Module [package="Breakout board"]
  Mod2 = KY-004 Key Switch Module [package="Breakout board"]
  Mod3 = KY-004 Key Switch Module [package="Breakout board"]
  A1 = BBAA100043
  J1 = Piezo Speaker

nets:
  N1: Raspberry_Pi_2.GPIO2, Part1.SDA
  N2: Raspberry_Pi_2.GPIO3, Part1.SCL
  N3: Raspberry_Pi_2.GIPO21, Mod1.S
  N4: Raspberry_Pi_2.GIPO20, Mod2.S
  N5: Raspberry_Pi_2.GIPO16, Mod3.S
  N6: Raspberry_Pi_2.GIPO12, J1.pin2
  N7: Raspberry_Pi_2.GIPO7, A1.pin3
  N8: Raspberry_Pi_2.GIPO8, A1.pin2
  N9: Raspberry_Pi_2.GIPO25, A1.pin1
  GND: Raspberry_Pi_2.GND, Part1.GND, Mod1.-, Mod2.-, Mod3.-, A1.pin4, J1.pin1
  VIN: Raspberry_Pi_2.5V, Part1.VCC, Mod1.Vin, Mod2.Vin, Mod3.Vin

custom parts:
  LCD1602-I2C: A standard character display, usually with 2x16 characters. Comes in many colors with LCM1602 IIC attached.
  KY-004 Key Switch Module: Arduino Key Switch Module Keyes KY-004 is a push button that will output a high signal when pressed.
  BBAA100043: BBAA100043 traffic light module.
